# Fritzing sketch esquematico_sensor_com_mcp3008 (saved by Fritzing 0.9.3b)
breadboards: 1

parts:
  IC1 = MCP3008 8-channel 10-bit ADC [part_number=MCP3008]
  DHT11 = DHT11 Humitidy and Temperature Sensor
  MQ-135 = Gas Sensor Breakout Board
  Raspberry_Pi_Zero_W = Raspberry Pi Zero
  R4 = Resistor [tolerance=±5% resistance=10k package="0805 [SMD]"]
  R5 = Resistor [tolerance=±5% resistance=10k package="0805 [SMD]"]
  R6 = Resistor [tolerance=±5% resistance=10k package="0805 [SMD]"]
  R8 = Resistor [tolerance=±5% resistance=750k package="0805 [SMD]"]
  U10 = Hirose DF13 Series Header [part_number=DF13#-8P-1.25V package=DF13C-8P-1.25V]
  MQ-131 = Gas Sensor Breakout Board
  R9 = Resistor [tolerance=±5% resistance=300k package="1206 [SMD]"]
  R9_2 = Resistor [tolerance=±5% resistance=360k package="0805 [SMD]"]
  R10 = Resistor [tolerance=±5% resistance=10k package="0805 [SMD]"]
  Part1 = Adafruit_BMP280

nets:
  N1: IC1.no_name_yet#1, R4.Pin_1, R5.Pin_0
  N2: IC1.no_name_yet#2, R8.Pin_0, R9.Pin_1, R9_2.Pin_1
  GND: IC1.no_name_yet#9, IC1.no_name_yet#14, DHT11.GND, MQ-135.GND, Raspberry_Pi_Zero_W.GND, R6.Pin_1, R8.Pin_1, U10.7, MQ-131.GND, Part1.GND
  N3: IC1.no_name_yet#10, Raspberry_Pi_Zero_W.GIPO5
  N4: IC1.no_name_yet#11, Raspberry_Pi_Zero_W.GIPO10
  N5: IC1.no_name_yet#12, Raspberry_Pi_Zero_W.GIPO9
  N6: IC1.no_name_yet#13, Raspberry_Pi_Zero_W.GIPO11
  VDD: IC1.no_name_yet#15, IC1.no_name_yet#16, DHT11.VDD, Raspberry_Pi_Zero_W.3v3, R10.Pin_1, Part1.VIN, Part1.SDO/ADR, Part1.CS
  N7: DHT11.DATA, Raspberry_Pi_Zero_W.GIPO4, R10.Pin_0
  N8: MQ-135.AOUT, MQ-135.DOUT, R4.Pin_0
  5V: MQ-135.5V, Raspberry_Pi_Zero_W.5V, U10.8, MQ-131.DOUT, MQ-131.5V
  N9: Raspberry_Pi_Zero_W.GPIO2, Part1.SDI/SDA
  N10: Raspberry_Pi_Zero_W.GPIO3, Part1.SCK/SCL
  N11: R5.Pin_1, R6.Pin_0
  N12: MQ-131.AOUT, R9.Pin_0, R9_2.Pin_0

custom parts:
  DHT11 Humitidy and Temperature Sensor: DHT11 Humidity and Temperature Sensor
  Gas Sensor Breakout Board: Gas sensor breakout board. Input voltage is 5V. Sensor output is available in analog and digital.
  Adafruit_BMP280: Bosch has stepped up their game with their new BMP280 sensor, an environmental sensor with temperature, barometric pressure that is the next generation upgrade to the BMP085/BMP180/BMP183. This sensor is great for all sorts of weather sensing and can even be used in both I2C and SPI! This precision sensor from Bosch is the best low-cost, precision sensing solution for measuring barometric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
