# Fritzing sketch v2_esquematico_sensor (saved by Fritzing 0.9.4)
breadboards: 1

parts:
  U10 = Hirose DF13 Series Header [part_number=DF13#-8P-1.25V package=DF13C-8P-1.25V]
  M1 = BME280
  MCU1 = Raspberry Pi Zero

nets:
  N1: U10.4, MCU1.pin_10
  N2: U10.5, MCU1.pin_8
  N3: U10.7, M1.GND, MCU1.pin_6, MCU1.pin_34, MCU1.pin_39
  N4: U10.8, MCU1.pin_2, MCU1.pin_4
  N5: M1.VIN, MCU1.pin_17
  N6: M1.SCL, MCU1.pin_5
  N7: M1.SDA, MCU1.pin_3

custom parts:
  BME280: Temperature Humidity Barometric presure Sensor
